// Logisim project MOD6_Synchronous_Counter_logic_block.circ as structural Verilog: 1 circuit, main circuit main
module main (
  input  [2:0] Q_2_0,
  output [2:0] D_2_0
);

  ROM #(.addrWidth(3), .dataWidth(3)) rom_1 ();  // open: addr, data

  // Notes on the sheet:
  //   MOD-6 synchronous counter next-state lookup. Connect Q[2:0] from three D flip-flop outputs to the address input. Connect D[2:0] to the flip-flop D inputs. Use a shared clock and reset state 000. Unused states 110 and 111 recover to 000.
  //   contents of rom_1 (hex, n*v repeats v):
  //   0 1 1 2 2 3 3 4 4 5 5 0 6 0 7 0
endmodule
