// Logisim project Traffic_Light_Moore_FSM_logic_block.circ as structural Verilog: 1 circuit, main circuit main
module main (
  input  [2:0] STATE_2_0,
  output [8:0] D_2_0____A_G_A_Y_A_R_B_G_B_Y_B_R
);

  ROM #(.addrWidth(3), .dataWidth(9)) rom_1 ();  // open: addr, data

  // Notes on the sheet:
  //   Moore traffic-light FSM lookup block. Input STATE[2:0]; output bus bits [8:6]=next state D2,D1,D0 and [5:0]=A_G,A_Y,A_R,B_G,B_Y,B_R. This is the combinational next-state/output block; connect a 3-bit D flip-flop state register with common clock and reset to make the complete sequential FSM.
  //   contents of rom_1 (hex, n*v repeats v):
  //   0 061 1 091 2 0C9 3 10C 4 14A 5 009 6 009 7 009
endmodule
